# Fritzing sketch Step002 (saved by Fritzing 0.9.2b)
breadboards: 1

parts:
  Part1 = Arduino Uno (Rev3) - ICSP
  DHT1 = DHT11 Humitidy and Temperature Sensor
  R1 = PHOTOCELL [package=photocell]
  R2 = Resistor [tolerance=±5% resistance=10k package=THT]
  R3 = Resistor [tolerance=±5% resistance=10k package=THT]
  LED1 = LED - 3mm [color="Red (633nm)" package="3 mm [THT]"]
  R4 = Resistor [tolerance=±5% resistance=220 package=THT]
  Raspberry_Pi_B_rev1 = Raspberry Pi B rev1

nets:
  N1: Part1.A3, R1.P$2, R2.Pin_0
  N2: Part1.A4/SDA, Raspberry_Pi_B_rev1.GPIO_0
  N3: Part1.A5/SCL, Raspberry_Pi_B_rev1.GPIO_1
  5V: Part1.5V, DHT1.VDD, R1.P$1, R3.Pin_1
  GND: Part1.GND, DHT1.GND, R2.Pin_1, LED1.cathode, Raspberry_Pi_B_rev1.GND
  N4: Part1.D1/TX, R4.Pin_1
  N5: Part1.D4, DHT1.DATA, R3.Pin_0
  N6: LED1.anode, R4.Pin_0

custom parts:
  DHT11 Humitidy and Temperature Sensor: DHT11 Humidity and Temperature Sensor

// code stored in the sketch: Test01.ino
#include "DHT.h"

#define PIN_DHT 4
#define PIN_PHOTORESISTOR A3
#define PIN_LED 1

#define debugCode 1

#define DHTTYPE DHT11   // DHT 11
//#define DHTTYPE DHT22   // DHT 22  (AM2302), AM2321
//#define DHTTYPE DHT21   // DHT 21 (AM2301)




float humidity = 0;
float temperatureCelsius = 0;
float temperatureFahrenheit = 0;
float heatIndexCelsius = 0;
float heatIndexFahrenheit = 0;
float lightLevelPercent = 0;

int photocellReading = 0;


// Initialize DHT sensor.
// Note that older versions of this library took an optional third parameter to
// tweak the timings for faster processors.  This parameter is no longer needed
// as the current DHT reading algorithm adjusts itself to work on faster procs.
DHT dht(PIN_DHT, DHTTYPE);

void setup() {
  pinMode(PIN_DHT, INPUT);
  pinMode(PIN_PHOTORESISTOR, INPUT);
  pinMode(PIN_LED, OUTPUT);

  digitalWrite(PIN_LED, LOW);

  if (debugCode) {
    Serial.begin(9600);
    while (!Serial) {
      ; // wait for serial port to connect. Needed for native USB
    }
    Serial.println("DHTxx test!");
  }
  dht.begin();
}

void loop() {
  // Wait a few seconds between measurements.
  delay(2000);
  digitalWrite(PIN_LED, HIGH);
  ReadDHT();
  ReadLightLevel();
  if (debugCode) {
    PrintDebug();
  }
  digitalWrite(PIN_LED, LOW);
}

void ReadDHT() {
  humidity = 0;
  temperatureCelsius = 0;
  temperatureFahrenheit = 0;
  heatIndexCelsius = 0;
  heatIndexFahrenheit = 0;

  // Reading temperature or humidity takes about 250 milliseconds!
  // Sensor readings may also be up to 2 seconds 'old' (its a very slow sensor)
  humidity = dht.readHumidity();
  // Read temperature as Celsius (the default)
  temperatureCelsius = dht.readTemperature();
  // Read temperature as Fahrenheit (isFahrenheit = true)
  temperatureFahrenheit = dht.readTemperature(true);

  // Check if any reads failed and exit early (to try again).
  if (isnan(humidity) || isnan(temperatureCelsius) || isnan(temperatureFahrenheit)) {
    Serial.println("Failed to read from DHT sensor!");
    return;
  }

  // Compute heat index in Fahrenheit (the default)
  heatIndexFahrenheit = dht.computeHeatIndex(temperatureFahrenheit, humidity);
  // Compute heat index in Celsius (isFahreheit = false)
  heatIndexCelsius = dht.computeHeatIndex(temperatureCelsius, humidity, false);
}

void ReadLightLevel() {
  photocellReading = analogRead(PIN_PHOTORESISTOR);
  lightLevelPercent = ((float)photocellReading / 1023.0) * 100.0;
}

void PrintDebug() {
  Serial.print("Humidity: ");
  Serial.print(humidity);
  Serial.print(" %\t");
  Serial.print("Temperature: ");
  Serial.print(temperatureCelsius);
  Serial.print(" *C ");
  Serial.print(temperatureFahrenheit);
  Serial.print(" *F\t");
  Serial.print("Heat index: ");
  Serial.print(heatIndexCelsius);
  Serial.print(" *C ");
  Serial.print(heatIndexFahrenheit);
  Serial.print(" *F\t");
  Serial.print("Light Level: ");
  Serial.print(photocellReading);     // the raw analog reading
  Serial.print("\t");
  Serial.print(lightLevelPercent);     // the raw analog reading
  Serial.println(" %");
}
